// Logisim project ARQ1_17-09.circ as structural Verilog: 12 circuits, main circuit main
module main (
);

  ula ula_1 ();  // open: D, A, B, Overflow, in_4, zero, out_6
endmodule

module add_1 (
  input  A,
  input  B,
  input  C,
  output S,
  output Vai_1
);

  wire and_1_out, and_2_out, or_1_out, xor_1_out;

  xor xor_1 (xor_1_out, C, B);
  or or_1 (or_1_out, B, C);
  and and_1 (and_1_out, B, C);
  xor xor_2 (S, xor_1_out, A);
  and and_2 (and_2_out, or_1_out, A);
  or or_2 (Vai_1, and_2_out, and_1_out);
endmodule

module add_4 (
  input  [3:0] A,
  input  [3:0] B,
  output Overflow,
  output [3:0] out_4
);

  wire add_1_2_vai_1, add_1_3_vai_1, add_1_4_vai_1;

  add_1 add_1_1 (.Vai_1(Overflow), .B(A[3]), .C(add_1_2_vai_1), .S(out_4[3]), .A(B[3]));
  add_1 add_1_2 (.Vai_1(add_1_2_vai_1), .B(A[2]), .C(add_1_3_vai_1), .S(out_4[2]), .A(B[2]));
  add_1 add_1_3 (.Vai_1(add_1_3_vai_1), .B(A[1]), .C(add_1_4_vai_1), .S(out_4[1]), .A(B[1]));
  add_1 add_1_4 (.Vai_1(add_1_4_vai_1), .B(A[0]), .C(1'b0), .S(out_4[0]), .A(B[0]));
endmodule

module sub_1 (
  input  A,
  input  B,
  input  C,
  output S,
  output Vai_1
);

  wire and_1_out, and_2_out, or_1_out, xor_1_out;

  xor xor_1 (xor_1_out, C, B);
  or or_1 (or_1_out, B, C);
  and and_1 (and_1_out, B, C);
  xor xor_2 (S, xor_1_out, A);
  and and_2 (and_2_out, or_1_out, ~A);  // AND_Gate
  or or_2 (Vai_1, and_2_out, and_1_out);
endmodule

module sub_4 (
  input  [3:0] in_1,
  input  [3:0] in_2,
  output out_3,
  output [3:0] out_4
);

  wire sub_1_2_vai_1, sub_1_3_vai_1, sub_1_4_vai_1;

  sub_1 sub_1_1 (.Vai_1(out_3), .A(in_2[3]), .B(in_1[3]), .C(sub_1_3_vai_1), .S(out_4[3]));
  sub_1 sub_1_2 (.Vai_1(sub_1_2_vai_1), .A(in_2[1]), .B(in_1[1]), .C(sub_1_4_vai_1), .S(out_4[1]));
  sub_1 sub_1_3 (.Vai_1(sub_1_3_vai_1), .A(in_2[2]), .B(in_1[2]), .C(sub_1_2_vai_1), .S(out_4[2]));
  sub_1 sub_1_4 (.Vai_1(sub_1_4_vai_1), .A(in_2[0]), .B(in_1[0]), .C(1'b0), .S(out_4[0]));
endmodule

module rot_d (
  input  [3:0] in_1,
  input  [1:0] in_2,
  output [3:0] out_3
);

  wire and_1_out, and_2_out, and_3_out, and_4_out, and_5_out, and_6_out, and_7_out, and_8_out, and_9_out;

  and and_1 (and_1_out, in_1[3], ~in_2[1], ~in_2[0]);  // AND_Gate
  and and_2 (and_2_out, in_1[2], ~in_2[1], in_2[0]);  // AND_Gate
  and and_3 (and_3_out, in_1[1], in_2[1], ~in_2[0]);  // AND_Gate
  and and_4 (and_4_out, in_1[0], in_2[1], in_2[0]);
  and and_5 (and_5_out, in_1[2], ~in_2[1], ~in_2[0]);  // AND_Gate
  and and_6 (and_6_out, in_1[1], ~in_2[1], in_2[0]);  // AND_Gate
  and and_7 (and_7_out, in_1[0], in_2[1], ~in_2[0]);  // AND_Gate
  and and_8 (and_8_out, in_1[1], ~in_2[1], ~in_2[0]);  // AND_Gate
  and and_9 (and_9_out, in_1[0], ~in_2[1], in_2[0]);  // AND_Gate
  and and_10 (out_3[3], in_1[0], ~in_2[1], ~in_2[0]);  // AND_Gate
  or or_1 (out_3[2], and_8_out, and_9_out);
  or or_2 (out_3[0], and_1_out, and_2_out, and_3_out, and_4_out);
  or or_3 (out_3[1], and_5_out, and_6_out, and_7_out);
endmodule

// dec
module decoder (
  input  [2:0] in_1,
  output D0,
  output D1,
  output D2,
  output D3,
  output D4,
  output D5,
  output D6,
  output D7
);

  wire not_1_out, not_2_out, not_3_out, not_4_out, not_5_out, not_6_out, not_7_out, not_8_out, not_9_out,
       not_10_out, not_11_out, not_12_out;

  not not_1 (not_1_out, in_1[2]);
  not not_2 (not_2_out, in_1[1]);
  and and_1 (D0, not_1_out, not_2_out, not_3_out);
  not not_3 (not_3_out, in_1[0]);
  not not_4 (not_4_out, in_1[2]);
  not not_5 (not_5_out, in_1[1]);
  and and_2 (D1, not_4_out, not_5_out, in_1[0]);
  not not_6 (not_6_out, in_1[2]);
  and and_3 (D2, not_6_out, in_1[1], not_7_out);
  not not_7 (not_7_out, in_1[0]);
  not not_8 (not_8_out, in_1[2]);
  and and_4 (D3, not_8_out, in_1[1], in_1[0]);
  not not_9 (not_9_out, in_1[1]);
  and and_5 (D4, in_1[2], not_9_out, not_10_out);
  not not_10 (not_10_out, in_1[0]);
  and and_6 (D5, in_1[2], not_11_out, in_1[0]);
  not not_11 (not_11_out, in_1[1]);
  and and_7 (D6, in_1[2], in_1[1], not_12_out);
  not not_12 (not_12_out, in_1[0]);
  and and_8 (D7, in_1[2], in_1[1], in_1[0]);
endmodule

module buffer (
  input  [3:0] E,
  input  C,
  output [3:0] S
);

  assign S[3] = C ? E[3] : 1'bz;  // Controlled_Buffer controlled_buffer_1
  assign S[2] = C ? E[2] : 1'bz;  // Controlled_Buffer controlled_buffer_2
  assign S[1] = C ? E[1] : 1'bz;  // Controlled_Buffer controlled_buffer_3
  assign S[0] = C ? E[0] : 1'bz;  // Controlled_Buffer controlled_buffer_4
endmodule

module \not  (
  input  [3:0] E,
  output [3:0] S
);

  not not_1 (S[3], E[3]);
  not not_2 (S[2], E[2]);
  not not_3 (S[0], E[0]);
  not not_4 (S[1], E[1]);
endmodule

// or
module or_4bits (
  input  [3:0] A,
  input  [3:0] B,
  output [3:0] out_3
);

  or or_1 (out_3[2], A[2], B[2]);
  or or_2 (out_3[3], A[3], B[3]);
  or or_3 (out_3[1], A[1], B[1]);
  or or_4 (out_3[0], A[0], B[0]);
endmodule

module ula (
  input  D,
  input  [3:0] A,
  input  [3:0] B,
  input  [2:0] in_4,
  output Overflow,
  output [3:0] out_6,
  output zero
);

  wire add_4_1_overflow, and_1_out, and_2_out, decoder_1_d0, decoder_1_d1, decoder_1_d2, decoder_1_d3,
       decoder_1_d4, decoder_1_d5, decoder_1_d6, decoder_1_d7, not_2_out, sub_4_1_out_3;
  wire [3:0] add_4_1_out_4, buffer_7_s, not_1_s, or_4bits_1_out_3, rot_d_1_out_3, rot_e_1_out_3,
       sub_4_1_out_4;

  and and_1 (and_1_out, decoder_1_d2, sub_4_1_out_3);
  or or_1 (Overflow, and_1_out, and_2_out);
  and and_2 (and_2_out, add_4_1_overflow, decoder_1_d1);
  decoder decoder_1 (
    .in_1(in_4), .D0(decoder_1_d0), .D1(decoder_1_d1), .D2(decoder_1_d2), .D3(decoder_1_d3),
    .D4(decoder_1_d4), .D5(decoder_1_d5), .D6(decoder_1_d6), .D7(decoder_1_d7));
  buffer buffer_1 (.E(B), .C(decoder_1_d0), .S(out_6));
  add_4 add_4_1 (.B(B), .A(A), .Overflow(add_4_1_overflow), .out_4(add_4_1_out_4));
  buffer buffer_2 (.E(add_4_1_out_4), .C(decoder_1_d1), .S(out_6));
  sub_4 sub_4_1 (.in_2(A), .in_1(B), .out_3(sub_4_1_out_3), .out_4(sub_4_1_out_4));
  buffer buffer_3 (.E(sub_4_1_out_4), .C(decoder_1_d2), .S(out_6));
  or_4bits or_4bits_1 (.A(A), .B(B), .out_3(or_4bits_1_out_3));
  \not  not_1 (.E(B), .S(not_1_s));
  buffer buffer_4 (.E(not_1_s), .C(decoder_1_d4), .S(out_6));
  buffer buffer_5 (.E(or_4bits_1_out_3), .C(decoder_1_d3), .S(out_6));
  nor nor_1 (zero, out_6[0], out_6[1], out_6[2], out_6[3], decoder_1_d6, decoder_1_d7);
  rot_e rot_e_1 (.in_1(A), .in_2(B[1:0]), .out_3(rot_e_1_out_3));
  rot_d rot_d_1 (.in_1(A), .in_2(B[1:0]), .out_3(rot_d_1_out_3));
  buffer buffer_6 (.E(buffer_7_s), .C(decoder_1_d5), .S(out_6));
  not not_2 (not_2_out, D);
  buffer buffer_7 (.E(rot_e_1_out_3), .C(not_2_out), .S(buffer_7_s));
  buffer buffer_8 (.E(rot_d_1_out_3), .C(D), .S(buffer_7_s));
endmodule

module rot_e (
  input  [3:0] in_1,
  input  [1:0] in_2,
  output [3:0] out_3
);

  wire and_1_out, and_2_out, and_3_out, and_4_out, and_5_out, and_6_out, and_7_out, and_8_out, and_9_out;

  and and_1 (and_1_out, in_1[3], ~in_2[1], ~in_2[0]);  // AND_Gate
  and and_2 (and_2_out, in_1[2], ~in_2[1], in_2[0]);  // AND_Gate
  and and_3 (and_3_out, in_1[1], in_2[1], ~in_2[0]);  // AND_Gate
  and and_4 (and_4_out, in_1[0], in_2[1], in_2[0]);
  and and_5 (and_5_out, in_1[2], ~in_2[1], ~in_2[0]);  // AND_Gate
  and and_6 (and_6_out, in_1[1], ~in_2[1], in_2[0]);  // AND_Gate
  and and_7 (and_7_out, in_1[0], in_2[1], ~in_2[0]);  // AND_Gate
  and and_8 (and_8_out, in_1[1], ~in_2[1], ~in_2[0]);  // AND_Gate
  and and_9 (and_9_out, in_1[0], ~in_2[1], in_2[0]);  // AND_Gate
  and and_10 (out_3[0], in_1[0], ~in_2[1], ~in_2[0]);  // AND_Gate
  or or_1 (out_3[3], and_1_out, and_2_out, and_3_out, and_4_out);
  or or_2 (out_3[2], and_5_out, and_6_out, and_7_out);
  or or_3 (out_3[1], and_8_out, and_9_out);
endmodule
