// Logisim project ARQ1_20-08.circ as structural Verilog: 5 circuits, main circuit main
module main (
  input  in_1,
  input  in_2,
  input  in_3,
  output out_4,
  output out_5
);

  add_1 add_1_1 (.Vai_1(out_4), .A(in_1), .B(in_2), .C(in_3), .S(out_5));
endmodule

module add_1 (
  input  A,
  input  B,
  input  C,
  output S,
  output Vai_1
);

  wire and_1_out, and_2_out, or_1_out, xor_1_out;

  xor xor_1 (xor_1_out, C, B);
  or or_1 (or_1_out, B, C);
  and and_1 (and_1_out, B, C);
  xor xor_2 (S, xor_1_out, A);
  and and_2 (and_2_out, or_1_out, A);
  or or_2 (Vai_1, and_2_out, and_1_out);
endmodule

module add_4 (
  input  [3:0] A,
  input  [3:0] B,
  output Overflow,
  output [3:0] Soma
);

  wire add_1_2_vai_1, add_1_3_vai_1, add_1_4_vai_1;

  add_1 add_1_1 (.Vai_1(Overflow), .A(A[3]), .B(B[3]), .C(add_1_2_vai_1), .S(Soma[3]));
  add_1 add_1_2 (.Vai_1(add_1_2_vai_1), .A(A[2]), .B(B[2]), .C(add_1_3_vai_1), .S(Soma[2]));
  add_1 add_1_3 (.Vai_1(add_1_3_vai_1), .A(A[1]), .B(B[1]), .C(add_1_4_vai_1), .S(Soma[1]));
  add_1 add_1_4 (.Vai_1(add_1_4_vai_1), .A(A[0]), .B(B[0]), .C(1'b0), .S(Soma[0]));
endmodule

module sub_1 (
  input  A,
  input  B,
  input  C,
  output S,
  output Vai_1
);

  wire and_1_out, and_2_out, or_1_out, xor_1_out;

  xor xor_1 (xor_1_out, C, B);
  or or_1 (or_1_out, B, C);
  and and_1 (and_1_out, B, C);
  xor xor_2 (S, xor_1_out, A);
  and and_2 (and_2_out, or_1_out, ~A);  // AND_Gate
  or or_2 (Vai_1, and_2_out, and_1_out);
endmodule

module sub_4 (
  input  [3:0] in_1,
  input  [3:0] in_2,
  output out_3,
  output [3:0] out_4
);

  wire sub_1_2_vai_1, sub_1_3_vai_1, sub_1_4_vai_1;

  // Probe on in_2
  sub_1 sub_1_1 (.Vai_1(out_3), .A(in_2[3]), .B(in_1[3]), .C(sub_1_2_vai_1), .S(out_4[3]));
  sub_1 sub_1_2 (.Vai_1(sub_1_2_vai_1), .A(in_2[2]), .B(in_1[2]), .C(sub_1_3_vai_1), .S(out_4[2]));
  sub_1 sub_1_3 (.Vai_1(sub_1_3_vai_1), .A(in_2[1]), .B(in_1[1]), .C(sub_1_4_vai_1), .S(out_4[1]));
  // Probe on out_4
  sub_1 sub_1_4 (.Vai_1(sub_1_4_vai_1), .A(in_2[0]), .B(in_1[0]), .C(1'b0), .S(out_4[0]));
  // Probe on in_1
endmodule
