// Logisim project ARQ1_27-08.circ as structural Verilog: 6 circuits, main circuit main
module main (
  input  [3:0] in_1,
  input  [3:0] in_2,
  output out_3,
  output out_4,
  output [3:0] out_5,
  output [3:0] out_6,
  output [3:0] out_7
);

  add_4 add_4_1 (.B(in_2), .A(in_1), .Overflow(out_3), .Soma(out_5));
  sub_4 sub_4_1 (.in_2(in_1), .in_1(in_2), .out_3(out_4), .out_4(out_6));
  rot_d rot_d_1 (.in_1(in_1), .in_2(in_2[1:0]), .out_3(out_7));
endmodule

module add_1 (
  input  A,
  input  B,
  input  C,
  output S,
  output Vai_1
);

  wire and_1_out, and_2_out, or_1_out, xor_1_out;

  xor xor_1 (xor_1_out, C, B);
  or or_1 (or_1_out, B, C);
  and and_1 (and_1_out, B, C);
  xor xor_2 (S, xor_1_out, A);
  and and_2 (and_2_out, or_1_out, A);
  or or_2 (Vai_1, and_2_out, and_1_out);
endmodule

module add_4 (
  input  [3:0] A,
  input  [3:0] B,
  output Overflow,
  output [3:0] Soma
);

  wire add_1_1_p5, add_1_2_p5, add_1_3_p5;

  // add_1 add_1_1: pin names not known; wires that end beside it: Overflow, A[3], Soma[3], B[3], add_1_1_p5, A[2]
  // add_1 add_1_2: pin names not known; wires that end beside it: add_1_1_p5, A[2], Soma[2], B[2], add_1_2_p5, A[1]
  // add_1 add_1_3: pin names not known; wires that end beside it: add_1_2_p5, A[1], Soma[1], B[1], add_1_3_p5, A[0]
  // add_1 add_1_4: pin names not known; wires that end beside it: add_1_3_p5, A[0], Soma[0], B[0], 1'b0
endmodule

module sub_1 (
  input  A,
  input  B,
  input  C,
  output S,
  output Vai_1
);

  wire and_1_out, and_2_out, or_1_out, xor_1_out;

  xor xor_1 (xor_1_out, C, B);
  or or_1 (or_1_out, B, C);
  and and_1 (and_1_out, B, C);
  xor xor_2 (S, xor_1_out, A);
  and and_2 (and_2_out, or_1_out, ~A);  // AND_Gate
  or or_2 (Vai_1, and_2_out, and_1_out);
endmodule

module sub_4 (
  input  [3:0] in_1,
  input  [3:0] in_2,
  output out_3,
  output [3:0] out_4
);

  wire sub_1_2_vai_1, sub_1_3_vai_1, sub_1_4_vai_1;

  // Probe on in_2
  sub_1 sub_1_1 (.Vai_1(out_3), .A(in_2[3]), .B(in_1[3]), .C(sub_1_2_vai_1), .S(out_4[3]));
  sub_1 sub_1_2 (.Vai_1(sub_1_2_vai_1), .A(in_2[2]), .B(in_1[2]), .C(sub_1_3_vai_1), .S(out_4[2]));
  sub_1 sub_1_3 (.Vai_1(sub_1_3_vai_1), .A(in_2[1]), .B(in_1[1]), .C(sub_1_4_vai_1), .S(out_4[1]));
  // Probe on out_4
  sub_1 sub_1_4 (.Vai_1(sub_1_4_vai_1), .A(in_2[0]), .B(in_1[0]), .C(1'b0), .S(out_4[0]));
  // Probe on in_1
endmodule

module rot_d (
  input  [3:0] in_1,
  input  [1:0] in_2,
  output [3:0] out_3
);

  wire and_1_out, and_2_out, and_3_out, and_4_out, and_5_out, and_6_out, and_7_out, and_8_out, and_9_out;

  and and_1 (and_1_out, in_1[3], ~in_2[1], ~in_2[0]);  // AND_Gate
  and and_2 (and_2_out, in_1[2], ~in_2[1], in_2[0]);  // AND_Gate
  and and_3 (and_3_out, in_1[1], in_2[1], ~in_2[0]);  // AND_Gate
  and and_4 (and_4_out, in_1[0], in_2[1], in_2[0]);
  and and_5 (and_5_out, in_1[2], ~in_2[1], ~in_2[0]);  // AND_Gate
  and and_6 (and_6_out, in_1[1], ~in_2[1], in_2[0]);  // AND_Gate
  and and_7 (and_7_out, in_1[0], in_2[1], ~in_2[0]);  // AND_Gate
  and and_8 (and_8_out, in_1[1], ~in_2[1], ~in_2[0]);  // AND_Gate
  and and_9 (and_9_out, in_1[0], ~in_2[1], in_2[0]);  // AND_Gate
  and and_10 (out_3[0], in_1[0], ~in_2[1], ~in_2[0]);  // AND_Gate
  or or_1 (out_3[3], and_1_out, and_2_out, and_3_out, and_4_out);
  or or_2 (out_3[2], and_5_out, and_6_out, and_7_out);
  or or_3 (out_3[1], and_8_out, and_9_out);
endmodule
